// Logisim project Alarme.circ as structural Verilog: 1 circuit, main circuit main
module main (
  input  A,
  input  B,
  input  C,
  output out_4
);

  wire or_1_out;

  or or_1 (or_1_out, A, B);
  and and_1 (out_4, or_1_out, C);
  LED S (.in(out_4));

  // Notes on the sheet:
  //   sensor porta
  //   sensor janela
  //   arma/desarma
  //   sirene
endmodule
